# Fritzing sketch Micro (saved by Fritzing 0.9.9b)

parts:
  BAT4 = Battery Holders [package=lipo-1100mAh]
  BAT7 = Battery Holders [package=lipo-1100mAh]
  BAT8 = Battery Holders [package=lipo-1100mAh]
  J1 = Basic Servo
  J17 = Camdenboss CTB0158-4 [part_number=CTB0158-4 package=THT]
  J18 = Camdenboss CTB0158-3 [part_number=CTB0158-3 package=THT]
  Mod3 = KY-008 Laser Transmitter Module [package="Breakout board"]
  Компонент5 = Bluetooth HC-05 Macho
  J19 = Camdenboss CTB0158-3 [part_number=CTB0158-3 package=THT]
  J20 = Camdenboss CTB0158-3 [part_number=CTB0158-3 package=THT]
  Micro = Arduino Micro (Rev3)
  M5 = RioRand LM2596
  J2 = Basic Servo

nets:
  N1: BAT4.+, Micro.VIN, M5.Pin_1
  N2: BAT4.-, BAT7.+
  N3: BAT7.-, BAT8.+
  N4: BAT8.-, J17.terminal_3, J20.terminal_1, Micro.GND, M5.Pin_2
  N5: J1.gnd, J17.terminal_2
  N6: J1.vcc, J18.terminal_1
  N7: J1.pulse, Micro.D10_PWM/A10
  N8: J17.pin1, J17.pin2, J17.pin3, J17.pin4
  N9: J17.terminal_1, J2.gnd
  N10: J17.terminal_4, M5.Pin_4
  N11: J18.pin1, J18.pin2, J18.pin3
  N12: J18.terminal_2, J2.vcc
  N13: J18.terminal_3, M5.Pin_3
  N14: Mod3.S, Micro.D9_PWM/A9
  N15: Mod3.NC, J19.terminal_2
  N16: Mod3.-, J20.terminal_2
  N17: Компонент5.TXD, Micro.D1/TX
  N18: Компонент5.RXD, Micro.D0/RX
  N19: Компонент5.VCC, J19.terminal_3
  N20: Компонент5.GND, J20.terminal_3
  N21: J19.pin1, J19.pin2, J19.pin3
  N22: J19.terminal_1, Micro.5V
  N23: J20.pin1, J20.pin2, J20.pin3
  N24: Micro.D11_PWM, J2.pulse

notes:
  Bluetooth модуль. Соединение по Bluetooth с Raspberry Pi 4B
  Лазерный модуль. Указание мишени на которую наведена установка
  Аккумулятор. Источник питания турели
  Серводвигатель. Поворот турели по оси Ox
  Серводвигатель. Поворот турели по оси Oy
  DC DC Понижающий преобразователь. Понижает напряжение до 7в для питания сервоприводов
  Плата. Наводит турель по заданным координатам и выстреливает лучом лазера

custom parts:
  KY-008 Laser Transmitter Module: KY-008 Laser Transmitter Module, emits a dot shaped red laser beam.
