# Fritzing sketch h (saved by Fritzing 0.9.9b)

parts:
  Компонент1 = Arduino Micro (Rev3)
  J1 = Camdenboss CTB0158-3 [part_number=CTB0158-3 package=THT]
  J2 = Camdenboss CTB0158-3 [part_number=CTB0158-3 package=THT]
  J3 = Camdenboss CTB0158-6 [part_number=CTB0158-6 package=THT]
  J4 = Camdenboss CTB0158-6 [part_number=CTB0158-6 package=THT]
  BAT1 = Battery Holders [package=lipo-1100mAh]
  BAT2 = Battery Holders [package=lipo-1100mAh]
  BAT3 = Battery Holders [package=lipo-1100mAh]
  J6 = Basic Servo
  J7 = Basic Servo
  M1 = RioRand LM2596
  M2 = RioRand LM2596
  Mod1 = KY-008 Laser Transmitter Module [package="Breakout board"]
  Компонент2 = Bluetooth HC-05 Macho

nets:
  N1: Компонент1.D1/TX, Компонент2.TXD
  N2: Компонент1.D0/RX, Компонент2.RXD
  N3: Компонент1.GND, J1.terminal_1, J3.terminal_3
  N4: Компонент1.D5_PWM, J6.pulse
  N5: Компонент1.D6_PWM/A7, J7.pulse
  N6: Компонент1.D7, Mod1.S
  N7: Компонент1.VIN, J4.terminal_3
  N8: Компонент1.5V, J2.terminal_3
  N9: J1.pin1, J1.pin2, J1.pin3
  N10: J1.terminal_2, Компонент2.GND
  N11: J1.terminal_3, Mod1.-
  N12: J2.pin1, J2.pin2, J2.pin3
  N13: J2.terminal_1, Компонент2.VCC
  N14: J2.terminal_2, Mod1.NC
  N15: J3.pin1, J3.pin2, J3.pin3, J3.pin4, J3.pin5, J3.pin6
  N16: J3.terminal_1, J7.gnd
  N17: J3.terminal_2, J6.gnd
  N18: J3.terminal_4, BAT3.-
  N19: J3.terminal_5, BAT2.-
  N20: J3.terminal_6, BAT1.-
  N21: J4.pin1, J4.pin2, J4.pin3, J4.pin4, J4.pin5, J4.pin6
  N22: J4.terminal_1, M1.Pin_2
  N23: J4.terminal_2, M2.Pin_2
  N24: J4.terminal_4, BAT3.+
  N25: J4.terminal_5, BAT2.+
  N26: J4.terminal_6, BAT1.+

custom parts:
  KY-008 Laser Transmitter Module: KY-008 Laser Transmitter Module, emits a dot shaped red laser beam.
