# Fritzing sketch Принципиальная схема (saved by Fritzing 0.9.9b)
breadboards: 1

parts:
  Компонент1 = Arduino Micro (Rev3)
  Mod1 = KY-008 Laser Transmitter Module [package="Breakout board"]
  Компонент2 = Bluetooth HC-05 Macho
  J1 = Basic Servo
  J2 = Basic Servo
  M1 = RioRand LM2596
  U1 = LIPO-1000mAh [package=lipo-1000]
  U2 = LIPO-1000mAh [package=lipo-1000]
  U3 = LIPO-1000mAh [package=lipo-1000]
  J3 = Camdenboss CTB0158-3 [part_number=CTB0158-3 package=THT]
  J4 = Camdenboss CTB0158-3 [part_number=CTB0158-3 package=THT]
  J5 = Camdenboss CTB0158-3 [part_number=CTB0158-3 package=THT]
  J6 = Camdenboss CTB0158-4 [part_number=CTB0158-4 package=THT]

nets:
  N1: Компонент1.D1/TX, Компонент2.RXD
  N2: Компонент1.D0/RX, Компонент2.TXD
  N3: Компонент1.GND, M1.Pin_4, J5.terminal_3
  N4: Компонент1.D9_PWM/A9, Mod1.S
  N5: Компонент1.D10_PWM/A10, J1.pulse
  N6: Компонент1.D11_PWM, J2.pulse
  N7: Компонент1.VIN, M1.Pin_3, U1.+
  N8: Компонент1.5V, J4.terminal_1
  N9: Mod1.NC, J4.terminal_3
  N10: Mod1.-, J5.terminal_1
  N11: Компонент2.VCC, J4.terminal_2
  N12: Компонент2.GND, J5.terminal_2
  N13: J1.gnd, J6.terminal_2
  N14: J1.vcc, J3.terminal_2
  N15: J2.gnd, J6.terminal_1
  N16: J2.vcc, J3.terminal_1
  N17: M1.Pin_1, J3.terminal_3
  N18: M1.Pin_2, J6.terminal_4
  N19: U1.-, U2.+
  N20: U2.-, U3.+
  N21: U3.-, J6.terminal_3
  N22: J3.pin1, J3.pin2, J3.pin3
  N23: J4.pin1, J4.pin2, J4.pin3
  N24: J5.pin1, J5.pin2, J5.pin3
  N25: J6.pin1, J6.pin2, J6.pin3, J6.pin4

notes:
  Плата. Наводит турель по заданным координатам и выстреливает лучом лазера
  Аккумулятор. Источник питания турели
  Серводвигатель. Поворот турели по оси Oy
  Серводвигатель. Поворот турели по оси Ox
  DC DC Понижающий преобразователь. Понижает напряжение до 7в для питания сервоприводов
  Лазерный модуль. Указание мишени на которую наведена установка
  Bluetooth модуль. Соединение по Bluetooth с Raspberry Pi 4B

custom parts:
  KY-008 Laser Transmitter Module: KY-008 Laser Transmitter Module, emits a dot shaped red laser beam.
