# Fritzing sketch МС (saved by Fritzing 0.9.10b)

parts:
  S9 = Taiway 100-SP-X-T1 SPDT Miniature Toggle Switch [part_number=100-SP-X-T1-0-0-B1-M2 package=THT]
  R4 = Resistor [tolerance=±5% resistance=220 package="0402 [SMD]"]
  U16 = WS2812 RGB LED strip
  C28 = Ceramic Capacitor [capacitance="100 nF" voltage=35V package="0603 [SMD, multilayer]"]
  C29 = Ceramic Capacitor [capacitance="100 nF" voltage=35V package="0603 [SMD, multilayer]"]
  C30 = Ceramic Capacitor [capacitance="100 nF" voltage=35V package="0603 [SMD, multilayer]"]
  C31 = Ceramic Capacitor [capacitance="100 nF" voltage=35V package="0603 [SMD, multilayer]"]
  U17 = ESP32-38PinWide [part_number=ESP32-38PinWide]
  BAT16 = Battery Holders [package=lipo-1100mAh]
  BAT17 = Battery Holders [package=lipo-1100mAh]
  BAT18 = Battery Holders [package=lipo-1100mAh]
  M33 = RioRand LM2596
  Pololu_A6 = Pololu A4988 [package=SO16]
  M34 = DC Motor [voltage_(max)=6V voltage_(min)=3V]
  M35 = DC Motor [voltage_(max)=6V voltage_(min)=3V]
  M36 = DC Motor [voltage_(max)=6V voltage_(min)=3V]
  SERVO6 = Tower Pro SG90 servo [part_number=101246]
  A11 = MX1508
  A12 = MX1508
  M37 = Stepper Motor - Bipolar
  S10 = Hall Sensor [part_number=WSH130 package=TO92]
  S11 = Hall Sensor [part_number=WSH130 package=TO92]
  S12 = Hall Sensor [part_number=WSH130 package=TO92]
  S13 = Hall Sensor [part_number=WSH130 package=TO92]

nets:
  N1: S9.COM, U17.GPIO13
  N2: S9.L2, U17.3.3
  N3: R4.Pin_0, U16.DIN
  N4: R4.Pin_1, U17.GPIO9
  N5: C28.0, M34.pin_1, A12.Pin_10
  N6: C28.1, M34.pin_2, A12.Pin_9
  N7: C29.0, M36.pin_1, A12.Pin_8
  N8: C29.1, M36.pin_2, A12.Pin_7
  N9: C30.0, M35.pin_1, A11.Pin_10
  N10: C30.1, M35.pin_2, A11.Pin_9
  N11: C31.0, U17.VIN, M33.Pin_1
  N12: U17.GPIO36, A11.Pin_4
  N13: U17.GPIO39, A11.Pin_3
  N14: U17.GPIO34, A12.Pin_6
  N15: U17.GPIO35, A12.Pin_5
  N16: U17.GPIO32, A12.Pin_4
  N17: U17.GPIO33, A12.Pin_3
  N18: U17.GPIO25, Pololu_A6.DIR
  N19: U17.GPIO26, Pololu_A6.STEP
  N20: U17.GPIO27, Pololu_A6.MS1
  N21: U17.GPIO14, Pololu_A6.MS2
  N22: U17.GPIO12, Pololu_A6.MS3
  GND: U17.GND, M33.Pin_2, S10.GND, S11.GND
  N23: U17.GPIO8, SERVO6.Signal
  N24: U17.GPIO15, S12.OUT
  N25: U17.GPIO2, S11.OUT
  N26: U17.GPIO3, S13.OUT
  N27: U17.GPIO1, S10.OUT
  N28: BAT16.+, BAT17.-
  N29: BAT17.+, BAT18.-
  N30: BAT18.+, A12.Pin_1
  N31: M33.Pin_4, A12.Pin_2
  N32: Pololu_A6.RESET, Pololu_A6.SLEEP
  N33: Pololu_A6.1B, M37.D
  N34: Pololu_A6.1A, M37.B
  N35: Pololu_A6.2A, M37.C
  N36: Pololu_A6.2B, M37.A

notes:
  Li-Po 3s 11.1v 1100mAh - Осуществляет питание устройств
  MTC-102-E1 - для включения/ выключения всего устройства
  SG90 - Осуществляет переворот платформы подъемника для сброса игральных костей
  LM2596S - Понижает напряжение до 5в для питания RPi и ESP32
  OH49E - для позицию барабана в зоне загрузки
  OH49E - для позицию барабана в зоне выгрузки
  OH49E - Фиксирует положение лифта во время загрузки кубиков
  OH49E - Фиксирует положение лифта во время выгрузки кубиков
  WS2812b - Осуществляет декоративные функции
  ESP32 - Управляющий контролле, отправляет и принимает данные с датчиков. CC4 - выступает в роли блокировочного конденсатора
  MX1508 - Управляет двигателями постоянного тока DC1 и DC2
  MX1508 - Управляет двигателем постоянного тока DC3
  GA12-N20 - Приводит в движение барабан. CC1 - выступает в роли блокировочного конденсатора
  GA12-N20 - Приводит в движение нижний конвейер.CC2 - выступает в роли блокировочного конденсатора
  GA12-N20 - Приводит в движение верхний конвейер. CC3 - выступает в роли блокировочного конденсатора
  A4988 - Управляет шаговым двигателем NEMA17
  17HE15-1504S - Управляет бобиной подъемника

custom parts:
  WS2812 RGB LED strip: WS2812 strip
  ESP32-38PinWide: Generic 38-Pin ESP32 with wide format (only access to one side of pins on a breadboard) based on Stephen Lilley's HiLetgo ESP-WROOM-32 ESP32 ESP-32S Development Board.
  Tower Pro SG90 servo: Original file by John De Cristofaro http://www.adafruit.com/products/1449 Adafruit Feedback Servo (Small) Edited by: e-radionica.com 28/9/2015
  MX1508: MX1508 DC Motor Driver is a low-cost motor driver module that can control DC stepper motors of current rating up to 2A.
  Hall Sensor: A Hall Sensor
